# Fritzing sketch Шаблон электросхемы проекта Ивана (saved by Fritzing 0.9.3b)
breadboards: 1

parts:
  Часть1 = Arduino Uno (Rev3)
  VCC1 = Battery
  S1 = Toggle Switch [package=THT]
  Mod1 = MQ-7 breakout
  Grove1 = Grove OLED 128x96
  SP1 = SPEAKER [package=pcb_mount_speaker]
  Q1 = NPN-Transistor [package="TO92 [THT]"]

nets:
  N1: Часть1.D2, Q1.B
  N2: Часть1.D3_PWM, Mod1.DO
  N3: Часть1.D4, Mod1.AO
  N4: Часть1.D5_PWM, Grove1.SDA
  N5: Часть1.D6_PWM, Grove1.SCL
  GND: Часть1.GND, S1.L2, Mod1.GND, Grove1.GND, SP1.+
  VCC: Часть1.VIN, VCC1.+, Mod1.VCC, Grove1.VCC, Q1.C
  N6: VCC1.-, S1.L1
  N7: SP1.-, Q1.E

custom parts:
  MQ-7 breakout: MQ-5 gas sensor
