# Fritzing sketch Шаблон электросхемы (saved by Fritzing 0.9.3b)
breadboards: 1

parts:
  Mod1 = MQ-7 breakout
  Grove1 = Grove OLED 128x96
  SP1 = SPEAKER [package=pcb_mount_speaker]
  Q1 = NPN-Transistor [package="TO92 [THT]"]
  YwRobot_Power_Supply1 = YwRobot Breadboard Power Supply [part_number=545043]
  Часть2 = Arduino Nano (Rev3.0)

nets:
  N1: Mod1.DO, Часть2.A3
  N2: Mod1.AO, Часть2.A4
  N3: Grove1.GND, SP1.+, YwRobot_Power_Supply1.GND#11, YwRobot_Power_Supply1.GND#12
  N4: Grove1.VCC, Q1.C, YwRobot_Power_Supply1.VCC#5, YwRobot_Power_Supply1.VCC#6
  N5: Grove1.SDA, Часть2.A5
  N6: Grove1.SCL, Часть2.A6
  N7: SP1.-, Q1.E
  N8: Q1.B, Часть2.A2
  N9: YwRobot_Power_Supply1.VCC#9, YwRobot_Power_Supply1.VCC#10
  N10: YwRobot_Power_Supply1.GND#13, YwRobot_Power_Supply1.GND#14

custom parts:
  MQ-7 breakout: MQ-5 gas sensor
  YwRobot Breadboard Power Supply: The YwRobot Breadboard Power Supply (MB-V2) has two power rails; they can be 5V or 3V3. Power to the module can be provided through the female USB socket or through the A10 (female) 2.1mm power jack.
